# Fritzing sketch BeeHive (saved by Fritzing 1.0.6)
breadboards: 2

parts:
  A1 = featherS3
  A2 = GY-SHT30 Breakout

nets:
  N1: A1.Pin_4, A1.Pin_38
  N2: A1.Pin_18, A1.Pin_20
  N3: A1.Pin_21, A2.Pin_4
  N4: A1.Pin_22, A2.Pin_3
  N5: A1.Pin_29, A1.Pin_34
  N6: A1.Pin_30, A1.Pin_36

custom parts:
  featherS3: FeatherS3 is the latest in our super popular ESP32 based Feather boards.
